# Fritzing sketch temporizador (saved by Fritzing 0.9.3b)
breadboards: 1

parts:
  S1 = Pushbutton [package="[THT]"]
  S3 = Pushbutton [package=THT]
  J1 = Piezo Speaker
  Componente1 = Arduino Uno (Rev3) - ICSP
  R2 = Resistor [tolerance=±5% resistance=220 package=THT]
  LED1 = LED - 5mm [color="Red (633nm)" package="5 mm [THT]"]
  R3 = Resistor [tolerance=±5% resistance=220 package=THT]
  R4 = Resistor [tolerance=±5% resistance=220 package=THT]
  KEYPAD1 = Membrane Matrix Keypad
  Grove2 = Grove 4 Digit Display

nets:
  N1: S1.Pin_1, S1.Pin_2, Grove2.VCC
  N2: S1.Pin_3, S1.Pin_4, Componente1.D3_PWM, R3.Pin_0
  N3: S3.leg0, Componente1.5V
  N4: S3.leg1, Componente1.D4, R2.Pin_1
  N5: J1.pin1, LED1.cathode, R3.Pin_1, Grove2.GND
  N6: J1.pin2, Componente1.D2, R4.Pin_0
  N7: Componente1.ICSP_MOSI, Componente1.D11_PWM/MOSI, KEYPAD1.3
  N8: Componente1.D8, KEYPAD1.6
  N9: Componente1.D9_PWM, KEYPAD1.5
  N10: Componente1.D10_PWM/SS, KEYPAD1.4
  N11: Componente1.D12/MISO, KEYPAD1.2
  N12: Componente1.D13/SCK, KEYPAD1.1
  N13: Componente1.D5_PWM, Grove2.DIO
  N14: Componente1.D6_PWM, Grove2.CLK
  N15: Componente1.D7, KEYPAD1.7
  N16: Componente1.GND, R2.Pin_0
  N17: LED1.anode, R4.Pin_1

custom parts:
  Membrane Matrix Keypad: Membrane Matrix 3x4 Keypad
